# Fritzing sketch AutoCajon (saved by Fritzing 0.9.1b)
breadboards: 1

parts:
  元件1 = Arduino Uno (Rev3)
  L1 = Solenoid
  VCC1 = Battery
  U1 = RELAY-2 [package=relay-g5v]
  D1 = Diode [package=diode-hv]
  Q1 = NPN-Transistor [package="TO92 [THT]"]
  R1 = Resistor [tolerance=±5% resistance=1k package="1206 [SMD]"]
  U2 = RELAY-2 [package=relay-g5v]
  D2 = Diode [package=diode-hv]
  Q2 = NPN-Transistor [package="TO92 [THT]"]
  R2 = Resistor [tolerance=±5% resistance=1k package="1206 [SMD]"]

nets:
  N1: 元件1.D8, R1.Pin_0
  N2: 元件1.D9_PWM, R2.Pin_0
  N3: 元件1.5V, U1.2, U2.2
  N4: 元件1.GND, U1.1, Q1.E, U2.1
  N5: L1.pin1, U2.6
  N6: L1.pin2, U1.6
  N7: VCC1.+, U1.10, U2.10
  N8: U1.9, D1.A, Q1.B
  N9: Q1.C, R1.Pin_1
  N10: U2.9, D2.A, Q2.B
  N11: Q2.C, R2.Pin_1
