# Fritzing sketch PerfBoard_v1 (saved by Fritzing 0.9.1b)
perfboards: 1

parts:
  Power_plug1 = Power plug
  元件1 = Arduino Uno (Rev3)
  R1 = Resistor [tolerance=±5% resistance=220 package=THT]
  U2 = LM386 [package=dip08]
  R5 = Resistor [tolerance=±5% resistance=220 package=THT]
  K3 = Relay [part_number=FRS1B-S package=THT]
  D3 = Rectifier Diode [part_number=1N4001 package="300 mil [THT]"]
  R6 = Resistor [package="0402 [SMD]"]
  K4 = Relay [part_number=FRS1B-S package=THT]
  LED2 = smd LED [color="Red (633nm)" package="1206 [SMD]"]
  D4 = Rectifier Diode [part_number=1N4001 package="300 mil [THT]"]
  Q3 = NPN-Transistor [package="TO92 [THT]"]
  Q4 = NPN-Transistor [package="TO92 [THT]"]
  R7 = Resistor [package="0402 [SMD]"]
  K7 = Relay [part_number=FRS1B-S package=THT]
  LED4 = smd LED [color="Red (633nm)" package="1206 [SMD]"]
  D7 = Rectifier Diode [part_number=1N4001 package="300 mil [THT]"]
  Q7 = NPN-Transistor [package="TO92 [THT]"]
  Q8 = NPN-Transistor [package="TO92 [THT]"]
  R12 = Resistor [package="0402 [SMD]"]
  U4 = LM386 [package=dip08]
  R13 = Resistor [tolerance=±5% resistance=220 package=THT]
  K8 = Relay [part_number=FRS1B-S package=THT]
  D8 = Rectifier Diode [part_number=1N4001 package="300 mil [THT]"]
  R14 = Resistor [package="0402 [SMD]"]
  R15 = Resistor [tolerance=±5% resistance=220 package=THT]
  K9 = Relay [part_number=FRS1B-S package=THT]
  LED5 = smd LED [color="Red (633nm)" package="1206 [SMD]"]
  D9 = Rectifier Diode [part_number=1N4001 package="300 mil [THT]"]
  Q9 = NPN-Transistor [package="TO92 [THT]"]
  Q10 = NPN-Transistor [package="TO92 [THT]"]
  R16 = Resistor [package="0402 [SMD]"]
  U5 = LM386 [package=dip08]
  R17 = Resistor [tolerance=±5% resistance=220 package=THT]
  K10 = Relay [part_number=FRS1B-S package=THT]
  D10 = Rectifier Diode [part_number=1N4001 package="300 mil [THT]"]
  R18 = Resistor [package="0402 [SMD]"]
  R19 = Resistor [tolerance=±5% resistance=220 package=THT]

nets:
  GND: Power_plug1.GND, 元件1.GND, U4.+IN, U4.V-
  N1: 元件1.D8, R18.Pin_0
  N2: 元件1.D9_PWM, R16.Pin_0
  N3: 元件1.D10_PWM/SS, R17.Pin_0
  N4: 元件1.D11_PWM/MOSI, R5.Pin_0
  N5: 元件1.D12/MISO, R7.Pin_0
  N6: 元件1.D13/SCK, R6.Pin_0
  N7: 元件1.D5_PWM, R13.Pin_0
  N8: 元件1.D6_PWM, R12.Pin_0
  N9: 元件1.D7, R14.Pin_0
  N10: 元件1.5V, K4.COIL2, D4.cathode
  N11: R1.Pin_0, R5.Pin_1
  N12: R1.Pin_1, U2.V+, K4.B
  N13: U2.+IN, U2.V-
  N14: K3.COIL1, D3.anode, Q4.C
  N15: K3.C1, K3.C2, LED2.cathode
  N16: K3.COIL2, D3.cathode
  N17: R6.Pin_1, Q3.B
  N18: K4.COIL1, D4.anode, Q3.C
  N19: K4.C1, K4.C2, LED2.anode
  N20: Q4.B, R7.Pin_1
  N21: K7.COIL1, D7.anode, Q7.C
  N22: K7.C1, K7.C2, LED4.anode
  N23: K7.COIL2, D7.cathode, K9.COIL2, D9.cathode
  N24: K7.B, U4.V+, R15.Pin_1
  N25: LED4.cathode, K8.C1, K8.C2
  N26: Q7.B, R14.Pin_1
  N27: Q8.B, R12.Pin_1
  N28: Q8.C, K8.COIL1, D8.anode
  N29: R13.Pin_1, R15.Pin_0
  N30: K8.COIL2, D8.cathode
  N31: K9.COIL1, D9.anode, Q9.C
  N32: K9.C1, K9.C2, LED5.anode
  N33: K9.B, U5.V+, R19.Pin_1
  N34: LED5.cathode, K10.C1, K10.C2
  N35: Q9.B, R18.Pin_1
  N36: Q10.B, R16.Pin_1
  N37: Q10.C, K10.COIL1, D10.anode
  N38: U5.+IN, U5.V-
  N39: R17.Pin_1, R19.Pin_0
  N40: K10.COIL2, D10.cathode
