# Fritzing sketch PerfBoard_v2 (saved by Fritzing 0.9.1b)
perfboards: 1

parts:
  Power_plug1 = Power plug
  元件1 = Arduino Uno (Rev3)
  K3 = Relay [part_number=FRS1B-S package=THT]
  D3 = Rectifier Diode [part_number=1N4001 package="300 mil [THT]"]
  R6 = Resistor [package="0402 [SMD]"]
  K4 = Relay [part_number=FRS1B-S package=THT]
  LED2 = smd LED [color="Red (633nm)" package="1206 [SMD]"]
  D4 = Rectifier Diode [part_number=1N4001 package="300 mil [THT]"]
  Q3 = NPN-Transistor [package="TO92 [THT]"]
  Q4 = NPN-Transistor [package="TO92 [THT]"]
  R7 = Resistor [package="0402 [SMD]"]
  K7 = Relay [part_number=FRS1B-S package=THT]
  LED4 = smd LED [color="Red (633nm)" package="1206 [SMD]"]
  D7 = Rectifier Diode [part_number=1N4001 package="300 mil [THT]"]
  Q7 = NPN-Transistor [package="TO92 [THT]"]
  Q8 = NPN-Transistor [package="TO92 [THT]"]
  R12 = Resistor [package="0402 [SMD]"]
  K8 = Relay [part_number=FRS1B-S package=THT]
  D8 = Rectifier Diode [part_number=1N4001 package="300 mil [THT]"]
  R14 = Resistor [package="0402 [SMD]"]
  K9 = Relay [part_number=FRS1B-S package=THT]
  LED5 = smd LED [color="Red (633nm)" package="1206 [SMD]"]
  D9 = Rectifier Diode [part_number=1N4001 package="300 mil [THT]"]
  Q9 = NPN-Transistor [package="TO92 [THT]"]
  Q10 = NPN-Transistor [package="TO92 [THT]"]
  R16 = Resistor [package="0402 [SMD]"]
  K10 = Relay [part_number=FRS1B-S package=THT]
  D10 = Rectifier Diode [part_number=1N4001 package="300 mil [THT]"]
  R18 = Resistor [package="0402 [SMD]"]

nets:
  GND: Power_plug1.GND, 元件1.GND
  N1: 元件1.D8, R18.Pin_0
  N2: 元件1.D9_PWM, R16.Pin_0
  N3: 元件1.D12/MISO, R7.Pin_0
  N4: 元件1.D13/SCK, R6.Pin_0
  N5: 元件1.D6_PWM, R12.Pin_0
  N6: 元件1.D7, R14.Pin_0
  N7: 元件1.5V, K4.COIL2, D4.cathode
  N8: K3.COIL1, D3.anode, Q4.C
  N9: K3.C1, K3.C2, LED2.cathode
  N10: K3.COIL2, D3.cathode
  N11: K3.B, K4.B
  N12: R6.Pin_1, Q3.B
  N13: K4.COIL1, D4.anode, Q3.C
  N14: K4.C1, K4.C2, LED2.anode
  N15: Q4.B, R7.Pin_1
  N16: K7.COIL1, D7.anode, Q7.C
  N17: K7.C1, K7.C2, LED4.anode
  N18: K7.COIL2, D7.cathode, K9.COIL2, D9.cathode
  N19: K7.B, K8.B
  N20: LED4.cathode, K8.C1, K8.C2
  N21: Q7.B, R14.Pin_1
  N22: Q8.B, R12.Pin_1
  N23: Q8.C, K8.COIL1, D8.anode
  N24: K8.COIL2, D8.cathode
  N25: K9.COIL1, D9.anode, Q9.C
  N26: K9.C1, K9.C2, LED5.anode
  N27: K9.B, K10.B
  N28: LED5.cathode, K10.C1, K10.C2
  N29: Q9.B, R18.Pin_1
  N30: Q10.B, R16.Pin_1
  N31: Q10.C, K10.COIL1, D10.anode
  N32: K10.COIL2, D10.cathode
